// Logisim project componete_2_Multp.circ as structural Verilog: 1 circuit, main circuit main
module main (
  input  A0,
  input  A1,
  input  A2,
  input  A3,
  input  S1,
  input  S2,
  output Saida
);

  wire and_1_out, and_2_out, and_3_out, and_4_out, not_1_out, not_2_out, not_3_out, not_4_out;

  not not_1 (not_1_out, S1);
  not not_2 (not_2_out, S2);
  not not_3 (not_3_out, S1);
  not not_4 (not_4_out, S2);
  and and_1 (and_1_out, A0, not_1_out, not_2_out);
  and and_2 (and_2_out, A1, not_3_out, S2);
  and and_3 (and_3_out, A2, S1, not_4_out);
  and and_4 (and_4_out, A3, S1, S2);
  or or_1 (Saida, and_1_out, and_2_out, and_3_out, and_4_out);
endmodule
